# Fritzing sketch weather_station (saved by Fritzing 0.9.3b)
circuit board: 8.46667cm x 5.64444cm
breadboards: 1

parts:
  R1 = Resistor [tolerance=±5% resistance=100k package=THT]
  R2 = Resistor [tolerance=±5% resistance=100k package=THT]
  Start_on_Deep_Sleep_Wake = SPST Switch [package=switch-spst-smd-a]
  Power_for_MCU = SPST Switch [package=switch-spst-smd-a]
  Temp_Pres_Hum = prefix0000
  Battery_Charger = prefix0000 [chip_label=TP4056]
  18650_Lithium_Polymer_Battery = LIPO-2000mAh [package=lipo-2000]
  5V_Solar_Cell = SOLAR-IXYS [package=solarbit-12x1]
  Microcontroller_Unit = WeMos D1 Mini
  IR_Full_Light = adafruit
  Red_LED = LED - 5mm [color="Red (633nm)" package="5 mm [THT]"]
  Red = Resistor [tolerance=±5% resistance=470 package=THT]

nets:
  N1: R1.Pin_0, R2.Pin_1
  N2: R1.Pin_1, Battery_Charger.connector3, 18650_Lithium_Polymer_Battery.+
  N3: R2.Pin_0, Microcontroller_Unit.A0
  N4: Start_on_Deep_Sleep_Wake.P, Microcontroller_Unit.D0
  N5: Start_on_Deep_Sleep_Wake.S, Microcontroller_Unit.RST
  N6: Power_for_MCU.P, Microcontroller_Unit.5V
  N7: Power_for_MCU.S, Battery_Charger.connector2
  N8: Temp_Pres_Hum.connector0, Microcontroller_Unit.3V3, IR_Full_Light.connector8
  N9: Temp_Pres_Hum.connector1, Battery_Charger.connector4, Battery_Charger.connector5, 18650_Lithium_Polymer_Battery.-, Microcontroller_Unit.G, IR_Full_Light.connector7, Red_LED.cathode
  N10: Temp_Pres_Hum.connector2, Microcontroller_Unit.D1, IR_Full_Light.connector11
  N11: Temp_Pres_Hum.connector3, Microcontroller_Unit.D2, IR_Full_Light.connector10
  N12: Battery_Charger.connector0, Battery_Charger.connector1, 5V_Solar_Cell.A, 5V_Solar_Cell.C
  N13: Microcontroller_Unit.D6, Red.Pin_0
  N14: Red_LED.anode, Red.Pin_1
